# Fritzing sketch Digital Simulation Playground (saved by Fritzing 0.9.3b)
breadboards: 1

parts:
  Part1 = Breadboard Power Supply Board SMD
  R1 = Resistor [tolerance=±5% resistance=100k package=THT]
  R2 = Resistor [tolerance=±5% resistance=100k package=THT]
  R3 = Resistor [tolerance=±5% resistance=100k package=THT]
  J1 = female pin header, 6 pins [form="♀ (female)"]
  R7 = Resistor [tolerance=±5% resistance=100k package=THT]
  R9 = Resistor [tolerance=±5% resistance=100k package=THT]
  R10 = Resistor [tolerance=±5% resistance=100k package=THT]
  Q1 = NPN-Transistor [package="TO92 [THT]"]
  Q2 = NPN-Transistor [package="TO92 [THT]"]
  Q3 = NPN-Transistor [package="TO92 [THT]"]
  R11 = Resistor [tolerance=±5% resistance=1k package=THT]
  R12 = Resistor [tolerance=±5% resistance=1k package=THT]
  R13 = Resistor [tolerance=±5% resistance=1k package=THT]
  LED1 = LED - 5mm [color="Green (555nm)" package="5 mm [THT]"]
  LED2 = LED - 5mm [color="Green (555nm)" package="5 mm [THT]"]
  LED3 = LED - 5mm [color="Yellow (595nm)" package="5 mm [THT]"]
  R14 = Resistor [tolerance=±5% resistance=1M package=THT]
  R15 = Resistor [tolerance=±5% resistance=1M package=THT]
  S1 = Pushbutton [package="[SMD]"]
  S2 = Pushbutton [package="[SMD]"]
  C1 = Ceramic Capacitor [capacitance=100nF package="200 mil [THT, multilayer]"]
  C2 = Ceramic Capacitor [capacitance=100nF package="200 mil [THT, multilayer]"]

nets:
  N1: Part1.GND, LED1.cathode, LED2.cathode, LED3.cathode, R14.Pin_0, R15.Pin_0
  N2: Part1.VCC, R11.Pin_0, R12.Pin_0, R13.Pin_0, S1.Pin_1, S1.Pin_2, S2.Pin_1, S2.Pin_2, C1.0, C2.0
  N3: R1.Pin_0, R7.Pin_0
  N4: R1.Pin_1, J1.pin1
  N5: R2.Pin_0, R9.Pin_0
  N6: R2.Pin_1, J1.pin2
  N7: R3.Pin_0, R10.Pin_0
  N8: R3.Pin_1, J1.pin3
  N9: J1.pin4, R7.Pin_1, Q1.B
  N10: J1.pin5, R9.Pin_1, Q2.B
  N11: R10.Pin_1, Q3.B
  N12: Q1.E, LED1.anode
  N13: Q1.C, R11.Pin_1
  N14: Q2.E, LED2.anode
  N15: Q2.C, R12.Pin_1
  N16: Q3.E, LED3.anode
  N17: Q3.C, R13.Pin_1
  N18: R14.Pin_1, S1.Pin_3, S1.Pin_4, C1.1
  N19: R15.Pin_1, S2.Pin_3, S2.Pin_4, C2.1
